# Fritzing sketch AY-3-8912_AVR (saved by Fritzing 1.0.3b)
circuit board: 2.1484cm x 3.9cm
breadboards: 1

parts:
  IC1 = IC, DIP package, 28 pins [chip_label=IC]
  IC2 = IC, DIP package, 28 pins [chip_label=IC]
  27MHz = Resonator [frequency="16 Mhz" package=THT]
  R1 = Resistor [tolerance=±5% resistance=220 power=0.25W package="0805 [SMD]"]
  R2 = Resistor [tolerance=±5% resistance=220 power=0.25W package="0805 [SMD]"]
  R3 = Resistor [tolerance=±5% resistance=220 power=0.25W package="0805 [SMD]"]

nets:
  N1: IC1.pin5, R3.Pin_0
  N2: IC1.pin15, IC2.pin6
  N3: IC1.pin17, IC2.pin18
  N4: IC1.pin18, IC2.pin5
  N5: IC1.pin19, IC2.pin19
  N6: IC1.pin20, IC2.pin4
  N7: IC1.pin21, IC2.pin13
  N8: IC1.pin22, IC2.pin12
  N9: IC1.pin23, IC2.pin28
  N10: IC1.pin24, IC2.pin27
  N11: IC1.pin25, IC2.pin26
  N12: IC1.pin26, IC2.pin25
  N13: IC1.pin27, IC2.pin24
  N14: IC1.pin28, IC2.pin23
  N15: IC2.pin9, 27MHz.0
  N16: IC2.pin10, 27MHz.pin_1
  N17: IC2.pin15, R3.Pin_1
  N18: IC2.pin16, R2.Pin_1
  N19: IC2.pin17, R1.Pin_1
  N20: IC2.pin22, 27MHz.GND
