# Fritzing sketch OPLL-MIDISynth_byJCR (saved by Fritzing 1.0.3b)
circuit board: 8.46667cm x 5.64444cm
breadboards: 1

parts:
  Part1 = Arduino Nano (Rev3.0)
  Part2 = Arduino Pro Mini v13  # not connected
  TRS1 = Audio Jack (TRS) 3.5mm [package="4Ucon 08780 [THT]"]  # not connected
  VBUS = Pad [width=3.861254072099717 height=3.430979727001059 connect=center]  # not connected
  UM3567 = IC, DIP package, 24 pins [chip_label=IC]
  Power_plug1 = Power plug
  7805 = Voltage Regulator [package=78xxl]
  YM2413 = IC, DIP package, 18 pins [chip_label=IC]

nets:
  VIN: Part1.VIN, Power_plug1.VCC, 7805.IN
  GND: Part1.GND, Power_plug1.GND, 7805.GND
  N1: UM3567.pin1, UM3567.pin9, UM3567.pin20, YM2413.pin1
  N2: UM3567.pin2, YM2413.pin2
  N3: UM3567.pin3, YM2413.pin3
  N4: UM3567.pin4, YM2413.pin4
  N5: UM3567.pin6, YM2413.pin5
  N6: UM3567.pin7, YM2413.pin6
  N7: UM3567.pin8, YM2413.pin7
  N8: UM3567.pin10, YM2413.pin8
  N9: UM3567.pin11, YM2413.pin9
  N10: UM3567.pin13, YM2413.pin10
  N11: UM3567.pin14, YM2413.pin11
  N12: UM3567.pin15, YM2413.pin12
  N13: UM3567.pin16, YM2413.pin13
  N14: UM3567.pin18, YM2413.pin14
  N15: UM3567.pin19, YM2413.pin15
  N16: UM3567.pin21, YM2413.pin16
  N17: UM3567.pin22, YM2413.pin17
  N18: UM3567.pin23, YM2413.pin18

notes:
  USB
