# Fritzing sketch Mapper19_Pacmance (saved by Fritzing 1.0.3b)
circuit board: 9.00001cm x 5.68cm
breadboards: 1

parts:
  1-30 = Generic single row SMD female header - 30 pins [form="♀ (female)" package=THT]
  60-31 = Generic single row SMD female header - 30 pins [form="♀ (female)" package=THT]
  Pad1 = Solder Mask Keepout FC Cartridge Connector  # not connected
  Pad2 = Solder Mask Keepout FC Cartridge Connector  # not connected
  Part1 = Namco 129/163/175/340
  4_7nF = Ceramic Capacitor [capacitance=100nF voltage=35V package="100 mil [THT, multilayer]"]
  10K = Resistor [tolerance=±5% power=0.25W resistance=220 package=THT]
  IC1 = IC, DIP package, 28 pins [chip_label=IC]
  IC2 = IC, DIP package, 28 pins [chip_label=IC]

nets:
  N1: 1-30.pin2, Part1.24, IC1.pin23
  N2: 1-30.pin3, IC1.pin21
  N3: 1-30.pin4, IC1.pin24
  N4: 1-30.pin5, IC1.pin25
  N5: 1-30.pin6, IC1.pin3
  N6: 1-30.pin7, IC1.pin4
  N7: 1-30.pin8, IC1.pin5
  N8: 1-30.pin9, IC1.pin6
  N9: 1-30.pin10, IC1.pin7
  N10: 1-30.pin11, IC1.pin8
  N11: 1-30.pin12, IC1.pin9
  N12: 1-30.pin13, IC1.pin10
  N13: 1-30.pin14, Part1.29
  N14: 1-30.pin15, Part1.39
  N15: 1-30.pin17, Part1.33
  N16: 1-30.pin19, IC2.pin4
  N17: 1-30.pin20, IC2.pin5
  N18: 1-30.pin21, IC2.pin6
  N19: 1-30.pin22, IC2.pin7
  N20: 1-30.pin23, IC2.pin8
  N21: 1-30.pin24, IC2.pin9
  N22: 1-30.pin25, IC2.pin10
  N23: 1-30.pin26, IC2.pin11
  N24: 1-30.pin27, IC2.pin12
  N25: 1-30.pin28, IC2.pin13
  N26: 60-31.pin26, Part1.27
  N27: 60-31.pin27, Part1.26
  N28: 60-31.pin28, Part1.25, IC1.pin2
  N29: 60-31.pin29, Part1.30
  N30: Part1.1, 4_7nF.0, 10K.Pin_0
  N31: Part1.10, IC1.pin1
  N32: Part1.18, IC1.pin13

custom parts:
  Generic single row SMD female header - 30 pins: Generic single row SMD female header
  Solder Mask Keepout FC Cartridge Connector: 90-10.7
