# Fritzing sketch Mapper69_FME-7Discrete (saved by Fritzing 1.0.3b)
circuit board: 9.00001cm x 5.68cm
breadboards: 1

parts:
  1-30 = Generic single row SMD female header - 30 pins [form="♀ (female)" package=THT]
  60-31 = Generic single row SMD female header - 30 pins [form="♀ (female)" package=THT]  # not connected
  Pad1 = Solder Mask Keepout FC Cartridge Connector  # not connected
  Pad2 = Solder Mask Keepout FC Cartridge Connector  # not connected
  IC1 = IC, DIP package, 32 pins [chip_label=IC]
  IC2 = IC, DIP package, 32 pins [chip_label=IC]
  74LS191 = SO16 [chip_label=IC package=SO]
  74LS191_2 = SO16 [chip_label=IC package=SO]
  74LS191_3 = SO16 [chip_label=IC package=SO]
  74LS191_4 = SO16 [chip_label=IC package=SO]  # not connected
  74LS670 = SO16 [chip_label=IC package=SO]  # not connected
  74LS670_2 = SO16 [chip_label=IC package=SO]  # not connected
  74LS670_3 = SO16 [chip_label=IC package=SO]  # not connected
  74LS670_4 = SO16 [chip_label=IC package=SO]
  74LS670_5 = SO16 [chip_label=IC package=SO]
  IC3 = QFN-20-0.4MM [chip_label=IC package=QFN]  # not connected
  74LS161 = SO16 [chip_label=IC package=SO]  # not connected
  74LS139 = SO16 [chip_label=IC package=SO]  # not connected
  GAL = IC, DIP package, 20 pins [chip_label=IC]
  74LS32 = SO16 [chip_label=IC package=SO]  # not connected
  74LS86 = SO16 [chip_label=IC package=SO]  # not connected
  74LS74 = SO16 [chip_label=IC package=SO]  # not connected

nets:
  N1: 1-30.pin1, GAL.pin10
  N2: 1-30.pin6, IC1.pin5
  N3: 1-30.pin7, IC1.pin6
  N4: 1-30.pin8, IC1.pin7
  N5: 1-30.pin9, IC1.pin8
  N6: 1-30.pin10, IC1.pin9
  N7: 1-30.pin11, IC1.pin10
  N8: 1-30.pin12, IC1.pin11
  N9: 1-30.pin13, IC1.pin12
  N10: 1-30.pin16, IC1.pin16
  N11: 1-30.pin19, IC2.pin6
  N12: 1-30.pin20, IC2.pin7
  N13: 1-30.pin21, IC2.pin8
  N14: 1-30.pin22, IC2.pin9
  N15: 1-30.pin23, IC2.pin10
  N16: 1-30.pin24, IC2.pin11
  N17: 1-30.pin25, IC2.pin12
  N18: 1-30.pin26, IC2.pin13
  N19: 1-30.pin27, IC2.pin14
  N20: 1-30.pin28, IC2.pin15
  N21: 74LS191.1, 74LS191_2.1, GAL.pin2
  N22: 74LS191.14, GAL.pin4
  N23: 74LS191.15, 74LS191_2.15, GAL.pin1
  N24: 74LS191_2.4, 74LS191_3.4
  N25: 74LS191_2.13, 74LS191_3.14
  N26: 74LS191_2.16, GAL.pin20
  N27: 74LS670_4.9, 74LS670_5.9
  N28: 74LS670_4.10, 74LS670_5.10

custom parts:
  Generic single row SMD female header - 30 pins: Generic single row SMD female header
  Solder Mask Keepout FC Cartridge Connector: 90-10.7
