# Fritzing sketch Mapper85_DonkeyKongCountry4VRC7 (saved by Fritzing 1.0.3b)
circuit board: 9.00001cm x 5.68cm
breadboards: 1

parts:
  1-30 = Generic single row SMD female header - 30 pins [form="♀ (female)" package=THT]
  60-31 = Generic single row SMD female header - 30 pins [form="♀ (female)" package=THT]
  3_58MHz = Crystal [frequency="16 Mhz" package=SMD]
  3_9K = Resistor [tolerance=±5% power=0.25W resistance=220 package=THT]
  2_2K = Resistor [tolerance=±5% power=0.25W resistance=220 package=THT]
  IC3 = IC, DIP package, 32 pins [chip_label=IC]
  VRC7 = IC, DIP package, 48 pins [chip_label=IC]
  Pad1 = Pad [width=1.8450698756469115 height=2.0987357935497952 connect=center]
  Pad2 = Pad [width=1.8450698756469115 height=2.0987357935497952 connect=center]
  Pad3 = Pad [width=1.8450698756469115 height=2.0987357935497952 connect=center]
  18pf = Ceramic Capacitor [capacitance=100nF voltage=35V package="1206 [SMD, multilayer]"]
  18pf1 = Ceramic Capacitor [capacitance=100nF voltage=35V package="1206 [SMD, multilayer]"]
  IC2 = IC, DIP package, 32 pins [chip_label=IC]
  VPP = Generic single row SMD female header - 2 pins [form="♀ (female)" package=THT]
  VPP_2 = Generic single row SMD female header - 2 pins [form="♀ (female)" package=THT]
  Pad4 = Solder Mask Keepout FC Cartridge Connector  # not connected
  Pad5 = Solder Mask Keepout FC Cartridge Connector  # not connected
  1uF = Ceramic Capacitor [capacitance=100nF voltage=35V package="100 mil [THT, multilayer]"]
  240K = Resistor [tolerance=±5% power=0.25W resistance=220 package=THT]
  910 = Resistor [tolerance=±5% power=0.25W resistance=220 package=THT]
  4_3K = Resistor [tolerance=±5% power=0.25W resistance=220 package=THT]
  22uF = Ceramic Capacitor [capacitance=100nF voltage=35V package="100 mil [THT, multilayer]"]
  33K = Resistor [tolerance=±5% power=0.25W resistance=220 package=THT]
  4_7nF = Ceramic Capacitor [capacitance=100nF voltage=35V package="100 mil [THT, multilayer]"]
  2_2K_2 = Resistor [tolerance=±5% power=0.25W resistance=220 package=THT]
  27K = Resistor [tolerance=±5% power=0.25W resistance=220 package=THT]
  LM359 = LM 358 Dual Op-Amp [package="SO 08 [SMD]"]
  LM358 = LM 358 Dual Op-Amp [package="DIP8 [THT]"]

nets:
  N1: 1-30.pin1, IC3.pin16, Pad2.pad, 18pf.1, 18pf1.0
  N2: 1-30.pin2, IC3.pin25
  N3: 1-30.pin3, IC3.pin23
  N4: 1-30.pin4, IC3.pin26
  N5: 1-30.pin5, IC3.pin27
  N6: 1-30.pin6, IC3.pin5
  N7: 1-30.pin7, IC3.pin6
  N8: 1-30.pin8, IC3.pin7, VRC7.pin16
  N9: 1-30.pin9, IC3.pin8, VRC7.pin19
  N10: 1-30.pin10, IC3.pin9
  N11: 1-30.pin11, IC3.pin10
  N12: 1-30.pin12, IC3.pin11
  N13: 1-30.pin13, IC3.pin12
  N14: 1-30.pin14, VRC7.pin4
  N15: 1-30.pin15, VRC7.pin5
  N16: 1-30.pin16, VRC7.pin3, VRC7.pin46, IC2.pin16, IC2.pin22, IC2.pin24, 1uF.0, 910.Pin_1, 22uF.1, 33K.Pin_0, 4_7nF.1, 2_2K_2.Pin_0, LM359.connector3, LM358.connector3
  N17: 1-30.pin17, VRC7.pin1
  N18: 1-30.pin18, VRC7.pin6
  N19: 1-30.pin19, IC2.pin6
  N20: 1-30.pin20, IC2.pin7
  N21: 1-30.pin21, IC2.pin8
  N22: 1-30.pin22, IC2.pin9
  N23: 1-30.pin23, IC2.pin10
  N24: 1-30.pin24, IC2.pin11
  N25: 1-30.pin25, IC2.pin12
  N26: 1-30.pin26, IC2.pin13
  N27: 1-30.pin27, IC2.pin14
  N28: 1-30.pin28, IC2.pin15
  N29: 1-30.pin29, IC2.pin17
  N30: 1-30.pin30, 60-31.pin30, IC3.pin32, VRC7.pin42, IC2.pin31, IC2.pin32, VPP.pin2, VPP_2.pin2, 1uF.1, LM359.connector4, LM359.connector5, LM359.connector7, LM358.connector4, LM358.connector5, LM358.connector7
  N31: 60-31.pin1, IC2.pin18
  N32: 60-31.pin2, IC2.pin19
  N33: 60-31.pin3, IC2.pin20
  N34: 60-31.pin4, IC2.pin21
  N35: 60-31.pin5, VRC7.pin2
  N36: 60-31.pin6, VRC7.pin33
  N37: 60-31.pin7, VRC7.pin32
  N38: 60-31.pin8, VRC7.pin31
  N39: 60-31.pin9, IC2.pin26
  N40: 60-31.pin10, IC2.pin27
  N41: 60-31.pin11, IC2.pin5
  N42: 60-31.pin12, 60-31.pin13
  N43: 60-31.pin15, 3_9K.Pin_0, 2_2K.Pin_1
  N44: 60-31.pin16, 3_9K.Pin_1
  N45: 60-31.pin17, VRC7.pin45
  N46: 60-31.pin18, IC3.pin13, VRC7.pin7
  N47: 60-31.pin19, IC3.pin14, VRC7.pin8
  N48: 60-31.pin20, IC3.pin15, VRC7.pin9
  N49: 60-31.pin21, IC3.pin17, VRC7.pin10
  N50: 60-31.pin22, IC3.pin18, VRC7.pin11
  N51: 60-31.pin23, IC3.pin19, VRC7.pin12
  N52: 60-31.pin24, IC3.pin20, VRC7.pin13
  N53: 60-31.pin25, IC3.pin21, VRC7.pin14
  N54: 60-31.pin26, VRC7.pin29
  N55: 60-31.pin27, VRC7.pin28
  N56: 60-31.pin28, IC3.pin4, VRC7.pin27
  N57: 60-31.pin29, VRC7.pin47
  N58: 3_58MHz.pin_0, VRC7.pin18, Pad3.pad, 18pf1.1
  N59: 3_58MHz.pin_1, VRC7.pin17, Pad1.pad, 18pf.0
  N60: 2_2K.Pin_0, 240K.Pin_1, 910.Pin_0, LM359.connector0, LM358.connector0
  N61: IC3.pin1, VPP.pin1
  N62: IC3.pin2, VRC7.pin23
  N63: IC3.pin3, VRC7.pin22
  N64: IC3.pin22, IC3.pin24, VRC7.pin44
  N65: IC3.pin28, VRC7.pin20
  N66: IC3.pin29, VRC7.pin21
  N67: IC3.pin30, VRC7.pin25
  N68: IC3.pin31, VRC7.pin26
  N69: VRC7.pin34, IC2.pin23
  N70: VRC7.pin35, IC2.pin25
  N71: VRC7.pin36, IC2.pin4
  N72: VRC7.pin37, IC2.pin28
  N73: VRC7.pin38, IC2.pin29
  N74: VRC7.pin39, IC2.pin3
  N75: VRC7.pin40, IC2.pin2
  N76: VRC7.pin41, IC2.pin30
  N77: VRC7.pin43, 2_2K_2.Pin_1, 27K.Pin_1
  N78: IC2.pin1, VPP_2.pin1
  N79: 240K.Pin_0, 4_3K.Pin_0, LM359.connector1, LM358.connector1
  N80: 4_3K.Pin_1, 22uF.0
  N81: 33K.Pin_1, 4_7nF.0, 27K.Pin_0, LM359.connector2, LM358.connector2
  N82: LM359.connector6, LM358.connector6

notes:
  4 VRC7 Hack Repro PCB
  Designed by HeeminYT
  If you're going to
  use oscillator,
  fi ll two capacitors above,
  if you're going to use
  use resonator instead,
  just place it on
  the three contacts on the top
  ^ the debug pin

custom parts:
  Generic single row SMD female header - 30 pins: Generic single row SMD female header
  Generic single row SMD female header - 2 pins: Generic single row SMD female header
  Solder Mask Keepout FC Cartridge Connector: 90-10.7
