# Fritzing sketch MapperUNKNOWN_20in1 (saved by Fritzing 1.0.3b)
circuit board: 9.00001cm x 5.68cm
breadboards: 1

parts:
  1-30 = Generic single row SMD female header - 30 pins [form="♀ (female)" package=THT]
  60-31 = Generic single row SMD female header - 30 pins [form="♀ (female)" package=THT]  # not connected
  Pad1 = Solder Mask Keepout FC Cartridge Connector  # not connected
  Pad2 = Solder Mask Keepout FC Cartridge Connector  # not connected
  27C080 = IC, DIP package, 32 pins [chip_label=IC]
  xx64 = IC, DIP package, 28 pins [chip_label=IC]  # not connected
  74HC139N = 74HC139N [part_number=74HC139N package="DIP (Dual Inline) [THT]"]  # not connected
  74LS273 = IC, DIP package, 20 pins [chip_label=IC]  # not connected
  74LS153 = IC, DIP package, 16 pins [chip_label=IC]  # not connected
  74LS02 = IC, DIP package, 14 pins [chip_label=IC]  # not connected

nets:
  N1: 1-30.pin16, 27C080.pin16

custom parts:
  Generic single row SMD female header - 30 pins: Generic single row SMD female header
  Solder Mask Keepout FC Cartridge Connector: 90-10.7
